// Logisim project CPU.circ as structural Verilog: 9 circuits, main circuit main
module main (
);

  wire ALUsrc, and_1_out, clock_1_out, MemRead, MemtoReg, MemWrite, PCsrc, REGWrite, ula_1_zero;
  wire [3:0] AluCtrl;
  wire [31:0] adder_1_out, adder_2_out, banco_reg_32_1_s0, banco_reg_32_1_s1, immgen_1_s, multiplexer_1_out,
       multiplexer_2_out, multiplexer_3_out, PC_s, ram_1_dout, ram_2_dout, ula_1_s;

  Clock clock_1 (.out(clock_1_out));
  Reg_32 PC (.A(multiplexer_3_out), .CLK(clock_1_out), .WRT(1'b1), .S(PC_s));
  RAM #(.addrWidth(24), .dataWidth(32)) ram_1 (
    .addr(PC_s[23:0]), .oe(1'b1), .clk(clock_1_out), .dout(ram_1_dout));  // open: we, din
  Adder #(.width(32)) adder_1 (.a(PC_s), .b(32'h4), .out(adder_1_out));  // open: cin, cout
  Control control_1 (
    .opcode(ram_1_dout[6:0]), .MW(MemWrite), .AS(ALUsrc), .MtR(MemtoReg), .PS(PCsrc), .MR(MemRead),
    .RW(REGWrite));
  FUNCT_Center funct_center_1 (.Funct3(ram_1_dout[14:12]), .Funct7(ram_1_dout[31:25]), .Aluctrl(AluCtrl));
  IMMgen immgen_1 (.Instruction(ram_1_dout), .S(immgen_1_s));
  Banco_Reg_32 banco_reg_32_1 (
    .writeData(multiplexer_2_out), .WRT(REGWrite), .RD(ram_1_dout[11:7]), .RS1(ram_1_dout[19:15]),
    .RS2(ram_1_dout[24:20]), .CLK(clock_1_out), .S0(banco_reg_32_1_s0), .S1(banco_reg_32_1_s1));
  Adder #(.width(32)) adder_2 (.a(PC_s), .b(immgen_1_s), .out(adder_2_out));  // open: cin, cout
  Multiplexer #(.width(32)) multiplexer_1 (
    .in0(banco_reg_32_1_s1), .in1(immgen_1_s), .out(multiplexer_1_out), .sel(ALUsrc));
  Multiplexer #(.width(32)) multiplexer_2 (.in0(ram_2_dout), .in1(ula_1_s), .out(multiplexer_2_out), .sel(MemtoReg));
  ULA ula_1 (.A(banco_reg_32_1_s0), .ALUCtrl(AluCtrl), .B(multiplexer_1_out), .Zero(ula_1_zero), .S(ula_1_s));
  Multiplexer #(.width(32)) multiplexer_3 (
    .in0(adder_1_out), .in1(adder_2_out), .out(multiplexer_3_out), .sel(and_1_out));
  and and_1 (and_1_out, ula_1_zero, PCsrc);
  RAM #(.addrWidth(24), .dataWidth(32)) ram_2 (
    .addr(ula_1_s[23:0]), .we(MemWrite), .oe(MemRead), .clk(clock_1_out), .din(banco_reg_32_1_s1),
    .dout(ram_2_dout));
endmodule

module Banco_Reg_32 (
  input  [31:0] writeData,
  input  WRT,
  input  [4:0] RD,
  input  [4:0] RS1,
  input  [4:0] RS2,
  input  CLK,
  output [31:0] S0,
  output [31:0] S1
);

  wire demultiplexer_1_out0, W1, W2, W3, W4, W5, W6, W7, W8, W9, W10, W11, W12, W13, W14, W15, W16, W17, W18,
       W19, W20, W21, W22, W23, W24, W25, W26, W27, W28, W29, W30, W31;
  wire [31:0] R0, R1, R2, R3, R4, R5, R6, R7, R8, R9, R10, R11, R12, R13, R14, R15, R16, R17, R18, R19, R20,
       R21, R22, R23, R24, R25, R26, R27, R28, R29, R30, R31;

  Demultiplexer #(.select(5)) demultiplexer_1 (
    .out0(demultiplexer_1_out0), .out1(W1), .out2(W2), .out3(W3), .out4(W4), .out5(W5), .out6(W6), .out7(W7),
    .out8(W8), .out9(W9), .out10(W10), .out11(W11), .out12(W12), .out13(W13), .out14(W14), .out15(W15),
    .out16(W16), .out17(W17), .out18(W18), .out19(W19), .out20(W20), .out21(W21), .out22(W22), .out23(W23),
    .out24(W24), .out25(W25), .out26(W26), .out27(W27), .out28(W28), .out29(W29), .out30(W30), .out31(W31),
    .in(WRT), .sel(RD));
  Reg_32 u_r0 (.A(writeData), .CLK(CLK), .WRT(1'b0), .S(R0));
  Reg_32 u_r1 (.A(writeData), .CLK(CLK), .WRT(W1), .S(R1));
  Reg_32 u_r2 (.A(writeData), .CLK(CLK), .WRT(W2), .S(R2));
  Reg_32 u_r3 (.A(writeData), .CLK(CLK), .WRT(W3), .S(R3));
  Reg_32 u_r4 (.A(writeData), .CLK(CLK), .WRT(W4), .S(R4));
  Reg_32 u_r5 (.A(writeData), .CLK(CLK), .WRT(W5), .S(R5));
  Reg_32 u_r6 (.A(writeData), .CLK(CLK), .WRT(W6), .S(R6));
  Reg_32 u_r7 (.A(writeData), .CLK(CLK), .WRT(W7), .S(R7));
  Reg_32 u_r8 (.A(writeData), .CLK(CLK), .WRT(W8), .S(R8));
  Reg_32 u_r9 (.A(writeData), .CLK(CLK), .WRT(W9), .S(R9));
  Reg_32 u_r10 (.A(writeData), .CLK(CLK), .WRT(W10), .S(R10));
  Reg_32 u_r11 (.A(writeData), .CLK(CLK), .WRT(W11), .S(R11));
  Reg_32 u_r12 (.A(writeData), .CLK(CLK), .WRT(W12), .S(R12));
  Reg_32 u_r13 (.A(writeData), .CLK(CLK), .WRT(W13), .S(R13));
  Reg_32 u_r14 (.A(writeData), .CLK(CLK), .WRT(W14), .S(R14));
  Reg_32 u_r15 (.A(writeData), .CLK(CLK), .WRT(W15), .S(R15));
  Reg_32 u_r16 (.A(writeData), .CLK(CLK), .WRT(W16), .S(R16));
  Reg_32 u_r17 (.A(writeData), .CLK(CLK), .WRT(W17), .S(R17));
  Reg_32 u_r18 (.A(writeData), .CLK(CLK), .WRT(W18), .S(R18));
  Reg_32 u_r19 (.A(writeData), .CLK(CLK), .WRT(W19), .S(R19));
  Reg_32 u_r20 (.A(writeData), .CLK(CLK), .WRT(W20), .S(R20));
  Reg_32 u_r21 (.A(writeData), .CLK(CLK), .WRT(W21), .S(R21));
  Reg_32 u_r22 (.A(writeData), .CLK(CLK), .WRT(W22), .S(R22));
  Reg_32 u_r23 (.A(writeData), .CLK(CLK), .WRT(W23), .S(R23));
  Reg_32 u_r24 (.A(writeData), .CLK(CLK), .WRT(W24), .S(R24));
  Reg_32 u_r25 (.A(writeData), .CLK(CLK), .WRT(W25), .S(R25));
  Reg_32 u_r26 (.A(writeData), .CLK(CLK), .WRT(W26), .S(R26));
  Reg_32 u_r27 (.A(writeData), .CLK(CLK), .WRT(W27), .S(R27));
  Reg_32 u_r28 (.A(writeData), .CLK(CLK), .WRT(W28), .S(R28));
  Reg_32 u_r29 (.A(writeData), .CLK(CLK), .WRT(W29), .S(R29));
  Reg_32 u_r30 (.A(writeData), .CLK(CLK), .WRT(W30), .S(R30));
  Reg_32 u_r31 (.A(writeData), .CLK(CLK), .WRT(W31), .S(R31));
  Multiplexer #(.select(5), .width(32)) multiplexer_1 (
    .in0(R0), .in1(R1), .in2(R2), .in3(R3), .in4(R4), .in5(R5), .in6(R6), .in7(R7), .in8(R8), .in9(R9),
    .in10(R10), .in11(R11), .in12(R12), .in13(R13), .in14(R14), .in15(R15), .in16(R16), .in17(R17),
    .in18(R18), .in19(R19), .in20(R20), .in21(R21), .in22(R22), .in23(R23), .in24(R24), .in25(R25),
    .in26(R26), .in27(R27), .in28(R28), .in29(R29), .in30(R30), .in31(R31), .out(S0), .sel(RS1));
  Multiplexer #(.select(5), .width(32)) multiplexer_2 (
    .in0(R0), .in1(R1), .in2(R2), .in3(R3), .in4(R4), .in5(R5), .in6(R6), .in7(R7), .in8(R8), .in9(R9),
    .in10(R10), .in11(R11), .in12(R12), .in13(R13), .in14(R14), .in15(R15), .in16(R16), .in17(R17),
    .in18(R18), .in19(R19), .in20(R20), .in21(R21), .in22(R22), .in23(R23), .in24(R24), .in25(R25),
    .in26(R26), .in27(R27), .in28(R28), .in29(R29), .in30(R30), .in31(R31), .out(S1), .sel(RS2));
  // also tied to GND on the sheet: demultiplexer_1_out0
endmodule

module Reg_32 (
  input  [31:0] A,
  input  CLK,
  input  WRT,
  output [31:0] S
);

  wire multiplexer_1_out, multiplexer_2_out, multiplexer_3_out, multiplexer_4_out, multiplexer_5_out,
       multiplexer_6_out, multiplexer_7_out, multiplexer_8_out, multiplexer_9_out, multiplexer_10_out,
       multiplexer_11_out, multiplexer_12_out, multiplexer_13_out, multiplexer_14_out, multiplexer_15_out,
       multiplexer_16_out, multiplexer_17_out, multiplexer_18_out, multiplexer_19_out, multiplexer_20_out,
       multiplexer_21_out, multiplexer_22_out, multiplexer_23_out, multiplexer_24_out, multiplexer_25_out,
       multiplexer_26_out, multiplexer_27_out, multiplexer_28_out, multiplexer_29_out, multiplexer_30_out,
       multiplexer_31_out, multiplexer_32_out;

  Multiplexer multiplexer_1 (.in0(S[0]), .in1(A[0]), .out(multiplexer_1_out), .sel(WRT));
  Multiplexer multiplexer_2 (.in0(S[1]), .in1(A[1]), .out(multiplexer_2_out), .sel(WRT));
  Multiplexer multiplexer_3 (.in0(S[2]), .in1(A[2]), .out(multiplexer_3_out), .sel(WRT));
  Multiplexer multiplexer_4 (.in0(S[3]), .in1(A[3]), .out(multiplexer_4_out), .sel(WRT));
  Multiplexer multiplexer_5 (.in0(S[4]), .in1(A[4]), .out(multiplexer_5_out), .sel(WRT));
  Multiplexer multiplexer_6 (.in0(S[5]), .in1(A[5]), .out(multiplexer_6_out), .sel(WRT));
  Multiplexer multiplexer_7 (.in0(S[6]), .in1(A[6]), .out(multiplexer_7_out), .sel(WRT));
  Multiplexer multiplexer_8 (.in0(S[7]), .in1(A[7]), .out(multiplexer_8_out), .sel(WRT));
  Multiplexer multiplexer_9 (.in0(S[8]), .in1(A[8]), .out(multiplexer_9_out), .sel(WRT));
  Multiplexer multiplexer_10 (.in0(S[9]), .in1(A[9]), .out(multiplexer_10_out), .sel(WRT));
  Multiplexer multiplexer_11 (.in0(S[10]), .in1(A[10]), .out(multiplexer_11_out), .sel(WRT));
  Multiplexer multiplexer_12 (.in0(S[11]), .in1(A[11]), .out(multiplexer_12_out), .sel(WRT));
  Multiplexer multiplexer_13 (.in0(S[12]), .in1(A[12]), .out(multiplexer_13_out), .sel(WRT));
  Multiplexer multiplexer_14 (.in0(S[13]), .in1(A[13]), .out(multiplexer_14_out), .sel(WRT));
  Multiplexer multiplexer_15 (.in0(S[14]), .in1(A[14]), .out(multiplexer_15_out), .sel(WRT));
  Multiplexer multiplexer_16 (.in0(S[15]), .in1(A[15]), .out(multiplexer_16_out), .sel(WRT));
  Multiplexer multiplexer_17 (.in0(S[16]), .in1(A[16]), .out(multiplexer_17_out), .sel(WRT));
  Multiplexer multiplexer_18 (.in0(S[17]), .in1(A[17]), .out(multiplexer_18_out), .sel(WRT));
  Multiplexer multiplexer_19 (.in0(S[18]), .in1(A[18]), .out(multiplexer_19_out), .sel(WRT));
  Multiplexer multiplexer_20 (.in0(S[19]), .in1(A[19]), .out(multiplexer_20_out), .sel(WRT));
  Multiplexer multiplexer_21 (.in0(S[20]), .in1(A[20]), .out(multiplexer_21_out), .sel(WRT));
  Multiplexer multiplexer_22 (.in0(S[21]), .in1(A[21]), .out(multiplexer_22_out), .sel(WRT));
  Multiplexer multiplexer_23 (.in0(S[22]), .in1(A[22]), .out(multiplexer_23_out), .sel(WRT));
  Multiplexer multiplexer_24 (.in0(S[23]), .in1(A[23]), .out(multiplexer_24_out), .sel(WRT));
  Multiplexer multiplexer_25 (.in0(S[24]), .in1(A[24]), .out(multiplexer_25_out), .sel(WRT));
  Multiplexer multiplexer_26 (.in0(S[25]), .in1(A[25]), .out(multiplexer_26_out), .sel(WRT));
  Multiplexer multiplexer_27 (.in0(S[26]), .in1(A[26]), .out(multiplexer_27_out), .sel(WRT));
  Multiplexer multiplexer_28 (.in0(S[27]), .in1(A[27]), .out(multiplexer_28_out), .sel(WRT));
  Multiplexer multiplexer_29 (.in0(S[28]), .in1(A[28]), .out(multiplexer_29_out), .sel(WRT));
  Multiplexer multiplexer_30 (.in0(S[29]), .in1(A[29]), .out(multiplexer_30_out), .sel(WRT));
  Multiplexer multiplexer_31 (.in0(S[30]), .in1(A[30]), .out(multiplexer_31_out), .sel(WRT));
  Multiplexer multiplexer_32 (.in0(S[31]), .in1(A[31]), .out(multiplexer_32_out), .sel(WRT));
  D_Flip_Flop d_ff_1 (.D(multiplexer_1_out), .clk(CLK), .Q(S[0]));  // open: Qn, preset, reset
  D_Flip_Flop d_ff_2 (.D(multiplexer_2_out), .Q(S[1]));  // open: clk, Qn, preset, reset
  D_Flip_Flop d_ff_3 (.D(multiplexer_3_out), .Q(S[2]));  // open: clk, Qn, preset, reset
  D_Flip_Flop d_ff_4 (.D(multiplexer_4_out), .Q(S[3]));  // open: clk, Qn, preset, reset
  D_Flip_Flop d_ff_5 (.D(multiplexer_5_out), .Q(S[4]));  // open: clk, Qn, preset, reset
  D_Flip_Flop d_ff_6 (.D(multiplexer_6_out), .Q(S[5]));  // open: clk, Qn, preset, reset
  D_Flip_Flop d_ff_7 (.D(multiplexer_7_out), .Q(S[6]));  // open: clk, Qn, preset, reset
  D_Flip_Flop d_ff_8 (.D(multiplexer_8_out), .Q(S[7]));  // open: clk, Qn, preset, reset
  D_Flip_Flop d_ff_9 (.D(multiplexer_9_out), .Q(S[8]));  // open: clk, Qn, preset, reset
  D_Flip_Flop d_ff_10 (.D(multiplexer_10_out), .Q(S[9]));  // open: clk, Qn, preset, reset
  D_Flip_Flop d_ff_11 (.D(multiplexer_11_out), .Q(S[10]));  // open: clk, Qn, preset, reset
  D_Flip_Flop d_ff_12 (.D(multiplexer_12_out), .Q(S[11]));  // open: clk, Qn, preset, reset
  D_Flip_Flop d_ff_13 (.D(multiplexer_13_out), .Q(S[12]));  // open: clk, Qn, preset, reset
  D_Flip_Flop d_ff_14 (.D(multiplexer_14_out), .Q(S[13]));  // open: clk, Qn, preset, reset
  D_Flip_Flop d_ff_15 (.D(multiplexer_15_out), .Q(S[14]));  // open: clk, Qn, preset, reset
  D_Flip_Flop d_ff_16 (.D(multiplexer_16_out), .Q(S[15]));  // open: clk, Qn, preset, reset
  D_Flip_Flop d_ff_17 (.D(multiplexer_17_out), .Q(S[16]));  // open: clk, Qn, preset, reset
  D_Flip_Flop d_ff_18 (.D(multiplexer_18_out), .Q(S[17]));  // open: clk, Qn, preset, reset
  D_Flip_Flop d_ff_19 (.D(multiplexer_19_out), .Q(S[18]));  // open: clk, Qn, preset, reset
  D_Flip_Flop d_ff_20 (.D(multiplexer_20_out), .Q(S[19]));  // open: clk, Qn, preset, reset
  D_Flip_Flop d_ff_21 (.D(multiplexer_21_out), .Q(S[20]));  // open: clk, Qn, preset, reset
  D_Flip_Flop d_ff_22 (.D(multiplexer_22_out), .Q(S[21]));  // open: clk, Qn, preset, reset
  D_Flip_Flop d_ff_23 (.D(multiplexer_23_out), .Q(S[22]));  // open: clk, Qn, preset, reset
  D_Flip_Flop d_ff_24 (.D(multiplexer_24_out), .Q(S[23]));  // open: clk, Qn, preset, reset
  D_Flip_Flop d_ff_25 (.D(multiplexer_25_out), .Q(S[24]));  // open: clk, Qn, preset, reset
  D_Flip_Flop d_ff_26 (.D(multiplexer_26_out), .Q(S[25]));  // open: clk, Qn, preset, reset
  D_Flip_Flop d_ff_27 (.D(multiplexer_27_out), .Q(S[26]));  // open: clk, Qn, preset, reset
  D_Flip_Flop d_ff_28 (.D(multiplexer_28_out), .Q(S[27]));  // open: clk, Qn, preset, reset
  D_Flip_Flop d_ff_29 (.D(multiplexer_29_out), .Q(S[28]));  // open: clk, Qn, preset, reset
  D_Flip_Flop d_ff_30 (.D(multiplexer_30_out), .Q(S[29]));  // open: clk, Qn, preset, reset
  D_Flip_Flop d_ff_31 (.D(multiplexer_31_out), .Q(S[30]));  // open: clk, Qn, preset, reset
  D_Flip_Flop d_ff_32 (.D(multiplexer_32_out), .clk(CLK), .Q(S[31]));  // open: Qn, preset, reset
endmodule

module ULA (
  input  [31:0] A,
  input  [3:0] ALUCtrl,
  input  [31:0] B,
  output Zero,
  output [31:0] S
);

  wire [31:0] adder_1_out, and_1_out, or_1_out, subtractor_1_out;

  assign and_1_out = A & B;  // AND_Gate and_1, 32 bits wide
  assign or_1_out = A | A;  // OR_Gate or_1, 32 bits wide
  Adder #(.width(32)) adder_1 (.a(A), .b(B), .out(adder_1_out));  // open: cin, cout
  Subtractor #(.width(32)) subtractor_1 (.a(A), .b(B), .out(subtractor_1_out));  // open: bin, bout
  Multiplexer #(.select(4), .width(32)) multiplexer_1 (
    .in0(and_1_out), .in1(or_1_out), .in2({32{1'b0}}), .in3(adder_1_out), .in4({32{1'b0}}),
    .in5(subtractor_1_out), .in6({32{1'b0}}), .in7({32{1'b0}}), .in8({32{1'b0}}), .in9({32{1'b0}}),
    .in10({32{1'b0}}), .in11({32{1'b0}}), .in12({32{1'b0}}), .in13({32{1'b0}}), .in14({32{1'b0}}),
    .in15({32{1'b0}}), .out(S), .sel(ALUCtrl));
  Eh_Zero eh_zero_1 (.A(S), .S(Zero));
endmodule

module Eh_Zero (
  input  [31:0] A,
  output S
);

  wire or_1_out, or_2_out, or_3_out, or_4_out, or_5_out, or_6_out, or_7_out, or_8_out, or_9_out, or_10_out,
       or_11_out, or_12_out, or_13_out, or_14_out, or_15_out, or_16_out, or_17_out, or_18_out, or_19_out,
       or_20_out, or_21_out, or_22_out, or_23_out, or_24_out, or_25_out, or_26_out, or_27_out, or_28_out,
       or_29_out, or_30_out, or_31_out, or_32_out;

  or or_1 (or_1_out, A[0], A[1]);
  or or_2 (or_2_out, A[2], A[3]);
  or or_3 (or_3_out, A[4], A[5]);
  or or_4 (or_4_out, A[6], A[7]);
  or or_5 (or_5_out, A[8], A[9]);
  or or_6 (or_6_out, A[10], A[11]);
  or or_7 (or_7_out, A[12], A[13]);
  or or_8 (or_8_out, A[14], A[15]);
  or or_9 (or_9_out, A[16], A[17]);
  or or_10 (or_10_out, A[18], A[19]);
  or or_11 (or_11_out, A[20], A[21]);
  or or_12 (or_12_out, A[22], A[23]);
  or or_13 (or_13_out, A[24], A[25]);
  or or_14 (or_14_out, A[26], A[27]);
  or or_15 (or_15_out, A[28], A[29]);
  or or_16 (or_16_out, A[30], A[31]);
  or or_17 (or_17_out, or_1_out, or_2_out);
  or or_18 (or_18_out, or_3_out, or_4_out);
  or or_19 (or_19_out, or_5_out, or_6_out);
  or or_20 (or_20_out, or_7_out, or_8_out);
  or or_21 (or_21_out, or_9_out, or_10_out);
  or or_22 (or_22_out, or_11_out, or_12_out);
  or or_23 (or_23_out, or_13_out, or_14_out);
  or or_24 (or_24_out, or_15_out, or_16_out);
  or or_25 (or_25_out, or_17_out, or_18_out);
  or or_26 (or_26_out, or_19_out, or_20_out);
  or or_27 (or_27_out, or_21_out, or_22_out);
  or or_28 (or_28_out, or_23_out, or_24_out);
  or or_29 (or_29_out, or_25_out, or_26_out);
  or or_30 (or_30_out, or_27_out, or_28_out);
  or or_31 (or_31_out, or_29_out, or_30_out);
  or or_32 (or_32_out, or_31_out, 1'b0);
  not not_1 (S, or_32_out);
endmodule

module IMMgen (
  input  [31:0] Instruction,
  output [31:0] S
);

  wire not_1_out;
  wire [31:0] ext_sig_1_out_2, ext_sig_2_out_2;

  not not_1 (not_1_out, Instruction[5]);
  Ext_Sig ext_sig_1 (.IMM(Instruction[31:20]), .out_2(ext_sig_1_out_2));
  Ext_Sig ext_sig_2 (.IMM({Instruction[31:25], Instruction[11:7]}), .out_2(ext_sig_2_out_2));
  Multiplexer #(.width(32)) multiplexer_1 (.in0(ext_sig_1_out_2), .in1(ext_sig_2_out_2), .out(S), .sel(not_1_out));
endmodule

module Ext_Sig (
  input  [11:0] IMM,
  output [31:0] out_2
);


  assign out_2 = {{21{IMM[11]}}, IMM[10:0]};
endmodule

module Control (
  input  [6:0] opcode,
  output MW,
  output AS,
  output MtR,
  output PS,
  output MR,
  output RW
);

  wire and_2_out, and_3_out, and_4_out, not_3_out, not_4_out, xnor_1_out;

  not not_1 (MtR, opcode[5]);
  xnor xnor_1 (xnor_1_out, opcode[5], opcode[4]);
  not not_2 (AS, opcode[4]);
  not not_3 (not_3_out, opcode[4]);
  and and_1 (RW, opcode[4], xnor_1_out);
  and and_2 (and_2_out, opcode[0], opcode[1]);
  and and_3 (and_3_out, opcode[5], not_3_out);
  not not_4 (not_4_out, opcode[5]);
  and and_4 (and_4_out, not_4_out, not_3_out);
  and and_5 (MW, and_2_out, and_3_out);
  and and_6 (MR, and_2_out, and_4_out);

  assign PS = opcode[6];
endmodule

module FUNCT_Center (
  input  [2:0] Funct3,
  input  [6:0] Funct7,
  output [3:0] Aluctrl
);

  wire nand_1_out, or_1_out, or_2_out, or_3_out, or_4_out, or_5_out, or_6_out, or_7_out, or_8_out, or_9_out;

  and and_1 (Aluctrl[0], Funct3[2], Funct3[1]);
  or or_1 (or_1_out, Funct3[0], Funct3[1]);
  or or_2 (or_2_out, Funct3[2], Funct7[0]);
  or or_3 (or_3_out, Funct7[1], Funct7[2]);
  or or_4 (or_4_out, Funct7[3], Funct7[4]);
  or or_5 (or_5_out, Funct7[5], Funct7[6]);
  nand nand_1 (nand_1_out, Funct3[0], Funct3[2]);
  and and_2 (Aluctrl[2], nand_1_out, Funct7[5]);
  or or_6 (or_6_out, or_1_out, or_2_out);
  or or_7 (or_7_out, or_3_out, or_4_out);
  or or_8 (or_8_out, or_6_out, or_9_out);
  or or_9 (or_9_out, or_7_out, or_5_out);
  or or_10 (Aluctrl[1], Aluctrl[2], or_8_out);

  assign Aluctrl[3] = 1'b0;
endmodule
