// Logisim project RISCV Monociclo.circ as structural Verilog: 6 circuits, main circuit main
module Banco_Reg (
  input  [31:0] rd,
  input  RegWrite,
  input  [4:0] rs1_endr,
  input  [4:0] rd_endr,
  input  CLK,
  input  [4:0] rs2_endr,
  output [31:0] rs1,
  output [31:0] rs2
);

  wire button_1_out, button_2_out, button_3_out, button_4_out, WeX0, WeX1, WeX2, WeX3, WeX4, WeX5, WeX6,
       WeX7, WeX8, WeX9, WeX10, WeX11, WeX12, WeX13, WeX14, WeX15, WeX16, WeX17, WeX18, WeX19, WeX20, WeX21,
       WeX22, WeX23, WeX24, WeX25, WeX26, WeX27, WeX28, WeX29, WeX30, WeX31;
  wire [31:0] x0q, x1q, x2q, x3q, x4q, x5q, x6q, x7q, x8q, x9q, x10q, x11q, x12q, x13q, x14q, x15q, x16q,
       x17q, x18q, x19q, x20q, x21q, x22q, x23q, x24q, x25q, x26q, x27q, x28q, x29q, x30q, x31q;

  Demultiplexer #(.select(5)) demultiplexer_1 (
    .out0(WeX0), .out1(WeX1), .out2(WeX2), .out3(WeX3), .out4(WeX4), .out5(WeX5), .out6(WeX6), .out7(WeX7),
    .out8(WeX8), .out9(WeX9), .out10(WeX10), .out11(WeX11), .out12(WeX12), .out13(WeX13), .out14(WeX14),
    .out15(WeX15), .out16(WeX16), .out17(WeX17), .out18(WeX18), .out19(WeX19), .out20(WeX20), .out21(WeX21),
    .out22(WeX22), .out23(WeX23), .out24(WeX24), .out25(WeX25), .out26(WeX26), .out27(WeX27), .out28(WeX28),
    .out29(WeX29), .out30(WeX30), .out31(WeX31), .in(RegWrite), .sel(rd_endr));
  Register #(.width(32)) x0 (.D({32{1'b0}}), .en(WeX0), .clk(CLK), .Q(x0q), .clr(button_1_out));
  Button button_1 (.out(button_1_out));
  Register #(.width(32)) x8 (.D(rd), .en(WeX8), .clk(CLK), .Q(x8q), .clr(button_2_out));
  Button button_2 (.out(button_2_out));
  Register #(.width(32)) x16 (.D(rd), .en(WeX16), .clk(CLK), .Q(x16q), .clr(button_3_out));
  Button button_3 (.out(button_3_out));
  Register #(.width(32)) x24 (.D(rd), .en(WeX24), .clk(CLK), .Q(x24q), .clr(button_4_out));
  Button button_4 (.out(button_4_out));
  Register #(.width(32)) x1 (.D(rd), .en(WeX1), .clk(CLK), .Q(x1q), .clr(button_1_out));
  Register #(.width(32)) x9 (.D(rd), .en(WeX9), .clk(CLK), .Q(x9q), .clr(button_2_out));
  Register #(.width(32)) x17 (.D(rd), .en(WeX17), .clk(CLK), .Q(x17q), .clr(button_3_out));
  Register #(.width(32)) x25 (.D(rd), .en(WeX25), .clk(CLK), .Q(x25q), .clr(button_4_out));
  Register #(.width(32)) x2 (.D(rd), .en(WeX2), .clk(CLK), .Q(x2q), .clr(button_1_out));
  Register #(.width(32)) x10 (.D(rd), .en(WeX10), .clk(CLK), .Q(x10q), .clr(button_2_out));
  Register #(.width(32)) x18 (.D(rd), .en(WeX18), .clk(CLK), .Q(x18q), .clr(button_3_out));
  Register #(.width(32)) x26 (.D(rd), .en(WeX26), .clk(CLK), .Q(x26q), .clr(button_4_out));
  Register #(.width(32)) x3 (.D(rd), .en(WeX3), .clk(CLK), .Q(x3q), .clr(button_1_out));
  Register #(.width(32)) x11 (.D(rd), .en(WeX11), .clk(CLK), .Q(x11q), .clr(button_2_out));
  Register #(.width(32)) x19 (.D(rd), .en(WeX19), .clk(CLK), .Q(x19q), .clr(button_3_out));
  Register #(.width(32)) x27 (.D(rd), .en(WeX27), .clk(CLK), .Q(x27q), .clr(button_4_out));
  Register #(.width(32)) x4 (.D(rd), .en(WeX4), .clk(CLK), .Q(x4q), .clr(button_1_out));
  Register #(.width(32)) x12 (.D(rd), .en(WeX12), .clk(CLK), .Q(x12q), .clr(button_2_out));
  Register #(.width(32)) x20 (.D(rd), .en(WeX20), .clk(CLK), .Q(x20q), .clr(button_3_out));
  Register #(.width(32)) x28 (.D(rd), .en(WeX28), .clk(CLK), .Q(x28q), .clr(button_4_out));
  Register #(.width(32)) x5 (.D(rd), .en(WeX5), .clk(CLK), .Q(x5q), .clr(button_1_out));
  Register #(.width(32)) x13 (.D(rd), .en(WeX13), .clk(CLK), .Q(x13q), .clr(button_2_out));
  Register #(.width(32)) x21 (.D(rd), .en(WeX21), .clk(CLK), .Q(x21q), .clr(button_3_out));
  Register #(.width(32)) x29 (.D(rd), .en(WeX29), .clk(CLK), .clr(button_4_out));  // open: Q
  Register #(.width(32)) x6 (.D(rd), .en(WeX6), .clk(CLK), .Q(x6q), .clr(button_1_out));
  Register #(.width(32)) x14 (.D(rd), .en(WeX14), .clk(CLK), .Q(x14q), .clr(button_2_out));
  Register #(.width(32)) x22 (.D(rd), .en(WeX22), .clk(CLK), .Q(x22q), .clr(button_3_out));
  Register #(.width(32)) x30 (.D(rd), .en(WeX30), .clk(CLK), .Q(x30q), .clr(button_4_out));
  Register #(.width(32)) x7 (.D(rd), .en(WeX7), .clk(CLK), .Q(x7q), .clr(button_1_out));
  Register #(.width(32)) x15 (.D(rd), .en(WeX15), .clk(CLK), .Q(x15q), .clr(button_2_out));
  Register #(.width(32)) x23 (.D(rd), .en(WeX23), .clk(CLK), .Q(x23q), .clr(button_3_out));
  Register #(.width(32)) x31 (.D(rd), .en(WeX31), .clk(CLK), .Q(x31q), .clr(button_4_out));
  Multiplexer #(.select(5), .width(32)) multiplexer_1 (
    .in0(x0q), .in1(x1q), .in2(x2q), .in3(x3q), .in4(x4q), .in5(x5q), .in6(x6q), .in7(x7q), .in8(x8q),
    .in9(x9q), .in10(x10q), .in11(x11q), .in12(x12q), .in13(x13q), .in14(x14q), .in15(x15q), .in16(x16q),
    .in17(x17q), .in18(x18q), .in19(x19q), .in20(x20q), .in21(x21q), .in22(x22q), .in23(x23q), .in24(x24q),
    .in25(x25q), .in26(x26q), .in27(x27q), .in28(x28q), .in29(x29q), .in30(x30q), .in31(x31q), .out(rs1),
    .sel(rs1_endr));
  Multiplexer #(.select(5), .width(32)) multiplexer_2 (
    .in0(x0q), .in1(x1q), .in2(x2q), .in3(x3q), .in4(x4q), .in5(x5q), .in6(x6q), .in7(x7q), .in8(x8q),
    .in9(x9q), .in10(x10q), .in11(x11q), .in12(x12q), .in13(x13q), .in14(x14q), .in15(x15q), .in16(x16q),
    .in17(x17q), .in18(x18q), .in19(x19q), .in20(x20q), .in21(x21q), .in22(x22q), .in23(x23q), .in24(x24q),
    .in25(x25q), .in26(x26q), .in27(x27q), .in28(x28q), .in29(x29q), .in30(x30q), .in31(x31q), .out(rs2),
    .sel(rs2_endr));
endmodule

module main (
);

  wire alu_1_eh_zero, ALUOp0, ALUOp1, ALUSrc, and_1_out, Branch, button_1_out, clk, control_1_memread,
       MemToReg, MemWrite, RegWrite;
  wire [2:0] Funct3;
  wire [3:0] aluctrl_1_operation;
  wire [6:0] Funct7;
  wire [23:0] adder_1_out, adder_2_out, bit_extender_1_out, bit_extender_2_out, multiplexer_2_out, PC_q;
  wire [24:0] rom_1_data;
  wire [31:0] alu_1_alu_result, banco_reg_1_rs1, banco_reg_1_rs2, imm_gen_1_saida, multiplexer_1_out,
       multiplexer_3_out, ram_1_dout;

  Register #(.width(24)) PC (.D(multiplexer_2_out), .en(1'b1), .clk(clk), .Q(PC_q), .clr(button_1_out));
  Button button_1 (.out(button_1_out));
  ROM #(.addrWidth(24), .dataWidth(32)) rom_1 (
    .addr(PC_q), .data({Funct7, rom_1_data[24:15], Funct3, rom_1_data[11:0]}));
  Clock clock_1 (.out(clk));
  IMM_Gen imm_gen_1 (
    .instrucao({Funct7, rom_1_data[24:15], Funct3, rom_1_data[11:0]}), .MemWrite(MemWrite), .Branch(Branch),
    .saida(imm_gen_1_saida));
  Control control_1 (
    .opcode(rom_1_data[6:0]), .RegWrite(RegWrite), .Branch(Branch), .MemRead(control_1_memread),
    .MemToReg(MemToReg), .MemWrite(MemWrite), .ALUSrc(ALUSrc), .ALUOp0(ALUOp0), .ALUOp1(ALUOp1));
  Banco_Reg banco_reg_1 (
    .rd(multiplexer_3_out), .RegWrite(RegWrite), .rs1_endr(rom_1_data[19:15]), .rd_endr(rom_1_data[11:7]),
    .CLK(clk), .rs2_endr(rom_1_data[24:20]), .rs1(banco_reg_1_rs1), .rs2(banco_reg_1_rs2));
  Bit_Extender #(.in_width(32), .out_width(24)) bit_extender_1 (.in(imm_gen_1_saida), .out(bit_extender_1_out));
  Multiplexer #(.width(32)) multiplexer_1 (
    .in0(banco_reg_1_rs2), .in1(imm_gen_1_saida), .out(multiplexer_1_out), .sel(ALUSrc));
  Adder #(.width(24)) adder_1 (.a(PC_q), .b(bit_extender_1_out), .out(adder_1_out));  // open: cin, cout
  Adder #(.width(24)) adder_2 (.a(24'h1), .b(PC_q), .out(adder_2_out));  // open: cin, cout
  Multiplexer #(.width(24)) multiplexer_2 (
    .in0(adder_2_out), .in1(adder_1_out), .out(multiplexer_2_out), .sel(and_1_out));
  and and_1 (and_1_out, Branch, alu_1_eh_zero);
  ALU alu_1 (
    .rs1(banco_reg_1_rs1), .seg_valor(multiplexer_1_out), .operation(aluctrl_1_operation),
    .ALU_Result(alu_1_alu_result), .eh_zero(alu_1_eh_zero));
  Bit_Extender #(.in_width(32), .out_width(24)) bit_extender_2 (.in(alu_1_alu_result), .out(bit_extender_2_out));
  ALUCtrl aluctrl_1 (
    .Funct7(Funct7), .Funct3(Funct3), .ALUOp1(ALUOp1), .ALUOp0(ALUOp0), .operation(aluctrl_1_operation));
  RAM #(.addrWidth(24), .dataWidth(32), .trigger("falling")) ram_1 (
    .addr(bit_extender_2_out), .we(MemWrite), .oe(control_1_memread), .clk(clk), .din(banco_reg_1_rs2),
    .dout(ram_1_dout));
  Multiplexer #(.width(32)) multiplexer_3 (
    .in0(alu_1_alu_result), .in1(ram_1_dout), .out(multiplexer_3_out), .sel(MemToReg));
endmodule

module ALU (
  input  [31:0] rs1,
  input  [31:0] seg_valor,
  input  [3:0] operation,
  output [31:0] ALU_Result,
  output eh_zero
);

  wire [4:0] bit_extender_1_out;
  wire [31:0] adder_1_out, and_1_out, or_1_out, shifter_1_out, subtractor_1_out;

  Bit_Extender #(.in_width(32), .out_width(5)) bit_extender_1 (.in(seg_valor), .out(bit_extender_1_out));
  Adder #(.width(32)) adder_1 (.a(rs1), .b(seg_valor), .out(adder_1_out));  // open: cin, cout
  Subtractor #(.width(32)) subtractor_1 (.a(rs1), .b(seg_valor), .out(subtractor_1_out));  // open: bin, bout
  assign and_1_out = seg_valor & seg_valor;  // AND_Gate and_1, 32 bits wide
  assign or_1_out = rs1 | seg_valor;  // OR_Gate or_1, 32 bits wide
  Shifter #(.width(32)) shifter_1 (.in(rs1), .\dist (bit_extender_1_out), .out(shifter_1_out));
  Comparator #(.width(32)) comparator_1 (.a(rs1), .b(seg_valor), .eq(eh_zero));  // open: gt, lt
  Multiplexer #(.select(4), .width(32)) multiplexer_1 (
    .in0(and_1_out), .in1(or_1_out), .in2(adder_1_out), .in3(shifter_1_out), .in6(subtractor_1_out),
    .out(ALU_Result), .sel(operation));  // open: in4, in5, in7, in8, in9, in10, in11, in12, in13, in14, in15
endmodule

module IMM_Gen (
  input  [31:0] instrucao,
  input  MemWrite,
  input  Branch,
  output [31:0] saida
);

  wire [11:0] multiplexer_1_out, shifter_1_out;

  Shifter #(.shift("ar"), .width(12)) shifter_1 (
    .in({instrucao[31], instrucao[11], instrucao[30:25], instrucao[10:7]}), .\dist (4'b0010),
    .out(shifter_1_out));
  Multiplexer #(.select(2), .width(12)) multiplexer_1 (
    .in0(instrucao[31:20]), .in1({instrucao[31:25], instrucao[11:7]}), .in2(shifter_1_out),
    .out(multiplexer_1_out), .sel({Branch, MemWrite}));  // open: in3
  assign saida = {{20{multiplexer_1_out[11]}}, multiplexer_1_out};  // Bit_Extender bit_extender_1

  // Notes on the sheet:
  //   00: IMM Tipo I | 01: IMM Tipo S | 10: IMM Tipo B
endmodule

module Control (
  input  [6:0] opcode,
  output RegWrite,
  output Branch,
  output MemRead,
  output MemToReg,
  output MemWrite,
  output ALUSrc,
  output ALUOp0,
  output ALUOp1
);

  wire and_1_out, and_2_out, and_3_out, and_8_out, and_9_out;

  and and_1 (and_1_out, ~opcode[6], ~opcode[5], opcode[4], ~opcode[3], ~opcode[2], opcode[1], opcode[0]);  // AND_Gate
  and and_2 (and_2_out, ~opcode[6], ~opcode[5], ~opcode[4], ~opcode[3], ~opcode[2], opcode[1], opcode[0]);  // AND_Gate
  and and_3 (and_3_out, ~opcode[6], opcode[5], opcode[4], ~opcode[3], ~opcode[2], opcode[1], opcode[0]);  // AND_Gate
  and and_4 (Branch, opcode[6], opcode[5], ~opcode[4], ~opcode[3], ~opcode[2], opcode[1], opcode[0]);  // AND_Gate
  and and_5 (MemRead, ~opcode[6], ~opcode[5], ~opcode[4], ~opcode[3], ~opcode[2], opcode[1], opcode[0]);  // AND_Gate
  and and_6 (MemToReg, ~opcode[6], ~opcode[5], ~opcode[4], ~opcode[3], ~opcode[2], opcode[1], opcode[0]);  // AND_Gate
  and and_7 (MemWrite, ~opcode[6], opcode[5], ~opcode[4], ~opcode[3], ~opcode[2], opcode[1], opcode[0]);  // AND_Gate
  and and_8 (and_8_out, ~opcode[6], ~opcode[5], ~opcode[4], ~opcode[3], ~opcode[2], opcode[1], opcode[0]);  // AND_Gate
  and and_9 (and_9_out, ~opcode[6], opcode[5], ~opcode[4], ~opcode[3], ~opcode[2], opcode[1], opcode[0]);  // AND_Gate
  and and_10 (ALUOp0, opcode[6], opcode[5], ~opcode[4], ~opcode[3], ~opcode[2], opcode[1], opcode[0]);  // AND_Gate
  or or_1 (RegWrite, and_2_out, and_1_out, and_3_out);
  or or_2 (ALUSrc, and_8_out, and_1_out, and_9_out);
  and and_11 (ALUOp1, opcode[0], opcode[1], ~opcode[2], ~opcode[3], opcode[4], opcode[5], ~opcode[6]);  // AND_Gate
endmodule

module ALUCtrl (
  input  [6:0] Funct7,
  input  [2:0] Funct3,
  input  ALUOp1,
  input  ALUOp0,
  output [3:0] operation
);

  wire and_1_out, and_2_out, and_3_out, and_4_out, and_5_out, and_6_out, and_7_out, and_8_out, and_9_out;

  and and_1 (and_1_out, ~Funct7[0], ~Funct7[1], ~Funct7[2], ~Funct7[3], ~Funct7[4], ~Funct7[5], ~Funct7[6], Funct3[0], ~Funct3[1], ~Funct3[2], ~ALUOp1, ~ALUOp0);  // AND_Gate
  and and_2 (and_2_out, ALUOp1, ~ALUOp0);  // AND_Gate
  and and_3 (and_3_out, Funct3[1], Funct3[2], ~Funct7[0], ~Funct7[1], ~Funct7[2], ~Funct7[3], ~Funct7[4], ~Funct7[5], ~Funct7[6], ~Funct3[0], ~ALUOp0, ALUOp1);  // AND_Gate
  and and_4 (and_4_out, ~Funct3[1], ~Funct3[1], ~Funct3[0], ~Funct7[6], ~Funct7[5], ~Funct7[4], ~Funct7[3], ~Funct7[2], ~Funct7[1], ~Funct7[0], ~and_2_out, ALUOp1);  // AND_Gate
  and and_5 (and_5_out, ~Funct3[0], ~Funct3[1], ~Funct3[2], ~Funct7[0], ~Funct7[1], ~Funct7[2], ~Funct7[3], ~Funct7[4], Funct7[5], ~Funct7[6], ~ALUOp0, ALUOp1);  // AND_Gate
  or or_1 (operation[0], and_1_out, and_3_out);
  and and_6 (and_6_out, ~Funct3[2], ~and_4_out, ~Funct3[1]);  // AND_Gate
  and and_7 (and_7_out, and_5_out, and_2_out);
  and and_8 (and_8_out, ~ALUOp1, ALUOp0);  // AND_Gate
  or or_2 (operation[2], and_7_out, and_8_out);
  and and_9 (and_9_out, ~ALUOp1, ~ALUOp1);  // AND_Gate
  or or_3 (operation[1], and_6_out, and_9_out);

  assign operation[3] = 1'b0;
endmodule
