// Logisim project RISCVPipeline.circ as structural Verilog: 14 circuits, main circuit main
module Banco_Reg (
  input  [31:0] rd,
  input  RegWrite,
  input  [4:0] rs1_endr,
  input  [4:0] rd_endr,
  input  CLK,
  input  [4:0] rs2_endr,
  output [31:0] rs1,
  output [31:0] rs2
);

  wire button_1_out, button_2_out, button_3_out, button_4_out, WeX0, WeX1, WeX2, WeX3, WeX4, WeX5, WeX6,
       WeX7, WeX8, WeX9, WeX10, WeX11, WeX12, WeX13, WeX14, WeX15, WeX16, WeX17, WeX18, WeX19, WeX20, WeX21,
       WeX22, WeX23, WeX24, WeX25, WeX26, WeX27, WeX28, WeX29, WeX30, WeX31;
  wire [31:0] x0q, x1q, x2q, x3q, x4q, x5q, x6q, x7q, x8q, x9q, x10q, x11q, x12q, x13q, x14q, x15q, x16q,
       x17q, x18q, x19q, x20q, x21q, x22q, x23q, x24q, x25q, x26q, x27q, x28q, x29q, x30q, x31q;

  Demultiplexer #(.select(5)) demultiplexer_1 (
    .out0(WeX0), .out1(WeX1), .out2(WeX2), .out3(WeX3), .out4(WeX4), .out5(WeX5), .out6(WeX6), .out7(WeX7),
    .out8(WeX8), .out9(WeX9), .out10(WeX10), .out11(WeX11), .out12(WeX12), .out13(WeX13), .out14(WeX14),
    .out15(WeX15), .out16(WeX16), .out17(WeX17), .out18(WeX18), .out19(WeX19), .out20(WeX20), .out21(WeX21),
    .out22(WeX22), .out23(WeX23), .out24(WeX24), .out25(WeX25), .out26(WeX26), .out27(WeX27), .out28(WeX28),
    .out29(WeX29), .out30(WeX30), .out31(WeX31), .in(RegWrite), .sel(rd_endr));
  Register #(.width(32)) x0 (.D({32{1'b0}}), .en(WeX0), .clk(CLK), .Q(x0q), .clr(button_1_out));
  Button button_1 (.out(button_1_out));
  Register #(.width(32)) x8 (.D(rd), .en(WeX8), .clk(CLK), .Q(x8q), .clr(button_2_out));
  Button button_2 (.out(button_2_out));
  Register #(.width(32)) x16 (.D(rd), .en(WeX16), .clk(CLK), .Q(x16q), .clr(button_3_out));
  Button button_3 (.out(button_3_out));
  Register #(.width(32)) x24 (.D(rd), .en(WeX24), .clk(CLK), .Q(x24q), .clr(button_4_out));
  Button button_4 (.out(button_4_out));
  Register #(.width(32)) x1 (.D(rd), .en(WeX1), .clk(CLK), .Q(x1q), .clr(button_1_out));
  Register #(.width(32)) x9 (.D(rd), .en(WeX9), .clk(CLK), .Q(x9q), .clr(button_2_out));
  Register #(.width(32)) x17 (.D(rd), .en(WeX17), .clk(CLK), .Q(x17q), .clr(button_3_out));
  Register #(.width(32)) x25 (.D(rd), .en(WeX25), .clk(CLK), .Q(x25q), .clr(button_4_out));
  Register #(.width(32)) x2 (.D(rd), .en(WeX2), .clk(CLK), .Q(x2q), .clr(button_1_out));
  Register #(.width(32)) x10 (.D(rd), .en(WeX10), .clk(CLK), .Q(x10q), .clr(button_2_out));
  Register #(.width(32)) x18 (.D(rd), .en(WeX18), .clk(CLK), .Q(x18q), .clr(button_3_out));
  Register #(.width(32)) x26 (.D(rd), .en(WeX26), .clk(CLK), .Q(x26q), .clr(button_4_out));
  Register #(.width(32)) x3 (.D(rd), .en(WeX3), .clk(CLK), .Q(x3q), .clr(button_1_out));
  Register #(.width(32)) x11 (.D(rd), .en(WeX11), .clk(CLK), .Q(x11q), .clr(button_2_out));
  Register #(.width(32)) x19 (.D(rd), .en(WeX19), .clk(CLK), .Q(x19q), .clr(button_3_out));
  Register #(.width(32)) x27 (.D(rd), .en(WeX27), .clk(CLK), .Q(x27q), .clr(button_4_out));
  Register #(.width(32)) x4 (.D(rd), .en(WeX4), .clk(CLK), .Q(x4q), .clr(button_1_out));
  Register #(.width(32)) x12 (.D(rd), .en(WeX12), .clk(CLK), .Q(x12q), .clr(button_2_out));
  Register #(.width(32)) x20 (.D(rd), .en(WeX20), .clk(CLK), .Q(x20q), .clr(button_3_out));
  Register #(.width(32)) x28 (.D(rd), .en(WeX28), .clk(CLK), .Q(x28q), .clr(button_4_out));
  Register #(.width(32)) x5 (.D(rd), .en(WeX5), .clk(CLK), .Q(x5q), .clr(button_1_out));
  Register #(.width(32)) x13 (.D(rd), .en(WeX13), .clk(CLK), .Q(x13q), .clr(button_2_out));
  Register #(.width(32)) x21 (.D(rd), .en(WeX21), .clk(CLK), .Q(x21q), .clr(button_3_out));
  Register #(.width(32)) x29 (.D(rd), .en(WeX29), .clk(CLK), .Q(x29q), .clr(button_4_out));
  Register #(.width(32)) x6 (.D(rd), .en(WeX6), .clk(CLK), .Q(x6q), .clr(button_1_out));
  Register #(.width(32)) x14 (.D(rd), .en(WeX14), .clk(CLK), .Q(x14q), .clr(button_2_out));
  Register #(.width(32)) x22 (.D(rd), .en(WeX22), .clk(CLK), .Q(x22q), .clr(button_3_out));
  Register #(.width(32)) x30 (.D(rd), .en(WeX30), .clk(CLK), .Q(x30q), .clr(button_4_out));
  Register #(.width(32)) x7 (.D(rd), .en(WeX7), .clk(CLK), .Q(x7q), .clr(button_1_out));
  Register #(.width(32)) x15 (.D(rd), .en(WeX15), .clk(CLK), .Q(x15q), .clr(button_2_out));
  Register #(.width(32)) x23 (.D(rd), .en(WeX23), .clk(CLK), .Q(x23q), .clr(button_3_out));
  Register #(.width(32)) x31 (.D(rd), .en(WeX31), .clk(CLK), .Q(x31q), .clr(button_4_out));
  Multiplexer #(.select(5), .width(32)) multiplexer_1 (
    .in0(x0q), .in1(x1q), .in2(x2q), .in3(x3q), .in4(x4q), .in5(x5q), .in6(x6q), .in7(x7q), .in8(x8q),
    .in9(x9q), .in10(x10q), .in11(x11q), .in12(x12q), .in13(x13q), .in14(x14q), .in15(x15q), .in16(x16q),
    .in17(x17q), .in18(x18q), .in19(x19q), .in20(x20q), .in21(x21q), .in22(x22q), .in23(x23q), .in24(x24q),
    .in25(x25q), .in26(x26q), .in27(x27q), .in28(x28q), .in29(x29q), .in30(x30q), .in31(x31q), .out(rs1),
    .sel(rs1_endr));
  Multiplexer #(.select(5), .width(32)) multiplexer_2 (
    .in0(x0q), .in1(x1q), .in2(x2q), .in3(x3q), .in4(x4q), .in5(x5q), .in6(x6q), .in7(x7q), .in8(x8q),
    .in9(x9q), .in10(x10q), .in11(x11q), .in12(x12q), .in13(x13q), .in14(x14q), .in15(x15q), .in16(x16q),
    .in17(x17q), .in18(x18q), .in19(x19q), .in20(x20q), .in21(x21q), .in22(x22q), .in23(x23q), .in24(x24q),
    .in25(x25q), .in26(x26q), .in27(x27q), .in28(x28q), .in29(x29q), .in30(x30q), .in31(x31q), .out(rs2),
    .sel(rs2_endr));
endmodule

module main (
);

  wire ALUOp0, ALUOp1, ALUSrc, and_1_out, and_2_out, Branch, button_1_out, clk, comparator_1_eq,
       control_1_aluop0, control_1_aluop1, control_1_alusrc, control_1_memread, control_1_memtoreg,
       control_1_regwrite, control_hazard_detector_1_stall, hazard_detection_1_stall, MemToReg, MEMtoRegEX,
       MemWrite, or_1_out, reg_ex_mem_1_memreadout, reg_ex_mem_1_memwriteout, reg_ex_mem_1_regwriteout,
       reg_id_ex_1_memreadout, reg_id_ex_1_memwriteout, reg_id_ex_1_regwriteout, reg_mem_wb_1_memtoregout,
       RegWrite, STALL;
  wire [1:0] forwarding_control_1_forward1, forwarding_control_1_forward2, fwd1, fwd2;
  wire [2:0] Funct3, reg_id_ex_1_funct3out;
  wire [3:0] aluctrl_1_operation;
  wire [4:0] RDEX, reg_ex_mem_1_rdout, reg_id_ex_1_rs1out, reg_id_ex_1_rs2out, reg_if_id_1_instout_2,
       reg_mem_wb_1_rdout, rs1, rs2;
  wire [6:0] Funct7, reg_id_ex_1_funct7out, reg_if_id_1_instout;
  wire [23:0] adder_1_out, adder_2_out, bit_extender_1_out, bit_extender_2_out, multiplexer_1_out, PC_q,
       reg_if_id_1_pcout;
  wire [31:0] alu_1_alu_result, AluRes, banco_reg_1_rs1, banco_reg_1_rs2, imm_gen_1_saida, multiplexer_2_out,
       multiplexer_3_out, multiplexer_4_out, multiplexer_5_out, multiplexer_6_out, multiplexer_7_out,
       multiplexer_8_out, ram_1_dout, reg_ex_mem_1_rs2out, reg_id_ex_1_immout, reg_id_ex_1_rs1dataout,
       reg_id_ex_1_rs2dataout, reg_mem_wb_1_aluresout, reg_mem_wb_1_memvalueout, rom_1_data;

  Adder #(.width(24)) adder_1 (.a(24'h1), .b(PC_q), .out(adder_1_out));  // open: cin, cout
  Register #(.width(24)) PC (.D(multiplexer_1_out), .en(and_1_out), .clk(clk), .Q(PC_q), .clr(button_1_out));
  Multiplexer #(.width(24)) multiplexer_1 (
    .in0(adder_1_out), .in1(adder_2_out), .out(multiplexer_1_out), .sel(and_2_out));
  and and_1 (and_1_out, STALL, ~control_hazard_detector_1_stall);  // AND_Gate
  ROM #(.addrWidth(24), .dataWidth(32)) rom_1 (.addr(PC_q), .data(rom_1_data));
  Button button_1 (.out(button_1_out));
  or or_1 (or_1_out, and_2_out, control_hazard_detector_1_stall);
  Clock clock_1 (.out(clk));
  Reg_IF_ID reg_if_id_1 (
    .Enable(STALL), .BranchStall(or_1_out), .PCin(PC_q), .Instin(rom_1_data), .CLK(clk),
    .PCout(reg_if_id_1_pcout),
    .Instout({Funct7, rs2, rs1, Funct3, reg_if_id_1_instout_2, reg_if_id_1_instout}));
  Control_Hazard_Detector control_hazard_detector_1 (
    .OPcode(rom_1_data[6:0]), .RS1(rom_1_data[19:15]), .RDID(reg_if_id_1_instout_2), .RS2(rom_1_data[24:20]),
    .RegWrite(control_1_regwrite), .MEMtoRegID(control_1_memtoreg), .RDEX(RDEX), .MEMtoRegEX(MEMtoRegEX),
    .STALL(control_hazard_detector_1_stall));
  Hazard_Detection hazard_detection_1 (
    .RS1(rs1), .MemRead(reg_id_ex_1_memreadout), .RDMem(RDEX), .RS2(rs2), .STALL(hazard_detection_1_stall));
  IMM_Gen imm_gen_1 (
    .instrucao({Funct7, rs2, rs1, Funct3, reg_if_id_1_instout_2, reg_if_id_1_instout}), .MemWrite(MemWrite),
    .Branch(Branch), .saida(imm_gen_1_saida));
  not not_1 (STALL, hazard_detection_1_stall);
  Control control_1 (
    .opcode(reg_if_id_1_instout), .RegWrite(control_1_regwrite), .Branch(Branch),
    .MemRead(control_1_memread), .MemToReg(control_1_memtoreg), .MemWrite(MemWrite),
    .ALUSrc(control_1_alusrc), .ALUOp0(control_1_aluop0), .ALUOp1(control_1_aluop1));
  Banco_Reg banco_reg_1 (
    .rd(multiplexer_8_out), .RegWrite(RegWrite), .rs1_endr(rs1), .rd_endr(reg_mem_wb_1_rdout), .CLK(clk),
    .rs2_endr(rs2), .rs1(banco_reg_1_rs1), .rs2(banco_reg_1_rs2));
  Multiplexer #(.select(2), .width(32)) multiplexer_2 (
    .in0(banco_reg_1_rs1), .in1(multiplexer_8_out), .in2(AluRes), .in3(AluRes), .out(multiplexer_2_out),
    .sel(forwarding_control_1_forward1));
  Multiplexer #(.select(2), .width(32)) multiplexer_3 (
    .in0(banco_reg_1_rs2), .in1(multiplexer_8_out), .in2(AluRes), .in3(AluRes), .out(multiplexer_3_out),
    .sel(forwarding_control_1_forward2));
  Comparator #(.width(32)) comparator_1 (
    .a(multiplexer_2_out), .b(multiplexer_3_out), .eq(comparator_1_eq));  // open: gt, lt
  Adder #(.width(24)) adder_2 (.a(reg_if_id_1_pcout), .b(bit_extender_1_out), .out(adder_2_out));  // open: cin, cout
  Bit_Extender #(.in_width(32), .out_width(24)) bit_extender_1 (.in(imm_gen_1_saida), .out(bit_extender_1_out));
  and and_2 (and_2_out, Branch, comparator_1_eq);
  Forwarding_Control forwarding_control_1 (
    .RS1(rs1), .RDWB(reg_mem_wb_1_rdout), .RegWriteWB(RegWrite), .RDMEM(reg_ex_mem_1_rdout),
    .REGWriteMEM(reg_ex_mem_1_regwriteout), .RS2(rs2), .Forward1(forwarding_control_1_forward1),
    .Forward2(forwarding_control_1_forward2));
  Reg_ID_EX reg_id_ex_1 (
    .STALL(hazard_detection_1_stall), .RegWritein(control_1_regwrite), .MemReadin(control_1_memread),
    .MemtoRegin(control_1_memtoreg), .MemWritein(MemWrite), .ALUSrcin(control_1_alusrc),
    .ALUOp0in(control_1_aluop0), .ALUOp1in(control_1_aluop1), .RDin(reg_if_id_1_instout_2),
    .RS1Datain(multiplexer_2_out), .RS2Datain(multiplexer_3_out), .IMMin(imm_gen_1_saida), .Funct7in(Funct7),
    .Fucnt3in(Funct3), .RS1in(rs1), .RS2in(rs2), .CLK(clk), .RegWriteout(reg_id_ex_1_regwriteout),
    .MemReadout(reg_id_ex_1_memreadout), .MemtoRegout(MEMtoRegEX), .MemWriteout(reg_id_ex_1_memwriteout),
    .ALUSrcout(ALUSrc), .ALUOp0out(ALUOp0), .ALUOp1out(ALUOp1), .RDout(RDEX),
    .RS1Dataout(reg_id_ex_1_rs1dataout), .RS2Dataout(reg_id_ex_1_rs2dataout), .IMMout(reg_id_ex_1_immout),
    .Funct7out(reg_id_ex_1_funct7out), .Funct3out(reg_id_ex_1_funct3out), .RS1out(reg_id_ex_1_rs1out),
    .RS2out(reg_id_ex_1_rs2out));
  Multiplexer #(.select(2), .width(32)) multiplexer_4 (
    .in0(reg_id_ex_1_rs2dataout), .in1(multiplexer_8_out), .in2(AluRes), .in3(AluRes),
    .out(multiplexer_4_out), .sel(fwd2));
  Multiplexer #(.select(2), .width(32)) multiplexer_5 (
    .in0(reg_id_ex_1_rs1dataout), .in1(multiplexer_8_out), .in2(AluRes), .in3(AluRes),
    .out(multiplexer_5_out), .sel(fwd1));
  Multiplexer #(.width(32)) multiplexer_6 (
    .in0(multiplexer_4_out), .in1(reg_id_ex_1_immout), .out(multiplexer_6_out), .sel(ALUSrc));
  Multiplexer #(.select(2), .width(32)) multiplexer_7 (
    .in0(reg_id_ex_1_rs2dataout), .in1(multiplexer_8_out), .in2(AluRes), .in3(AluRes),
    .out(multiplexer_7_out), .sel(fwd2));
  ALUCtrl aluctrl_1 (
    .Funct7(reg_id_ex_1_funct7out), .Funct3(reg_id_ex_1_funct3out), .ALUOp1(ALUOp1), .ALUOp0(ALUOp0),
    .operation(aluctrl_1_operation));
  ALU alu_1 (
    .rs1(multiplexer_5_out), .seg_valor(multiplexer_6_out), .operation(aluctrl_1_operation),
    .ALU_Result(alu_1_alu_result));
  Reg_EX_MEM reg_ex_mem_1 (
    .RegWritein(reg_id_ex_1_regwriteout), .MemReadin(reg_id_ex_1_memreadout), .MemtoRegin(MEMtoRegEX),
    .MemWritein(reg_id_ex_1_memwriteout), .RDin(RDEX), .ALUResin(alu_1_alu_result),
    .RS2in(multiplexer_7_out), .CLK(clk), .RegWriteout(reg_ex_mem_1_regwriteout),
    .MemReadout(reg_ex_mem_1_memreadout), .MemtoRegout(MemToReg), .MemWriteout(reg_ex_mem_1_memwriteout),
    .RDout(reg_ex_mem_1_rdout), .ALUResout(AluRes), .RS2out(reg_ex_mem_1_rs2out));
  Forwarding_Control forwarding_control_2 (
    .RS1(reg_id_ex_1_rs1out), .RDWB(reg_mem_wb_1_rdout), .RegWriteWB(RegWrite), .RDMEM(reg_ex_mem_1_rdout),
    .REGWriteMEM(reg_ex_mem_1_regwriteout), .RS2(reg_id_ex_1_rs2out), .Forward1(fwd1), .Forward2(fwd2));
  Bit_Extender #(.in_width(32), .out_width(24)) bit_extender_2 (.in(AluRes), .out(bit_extender_2_out));
  RAM #(.addrWidth(24), .dataWidth(32), .trigger("falling")) ram_1 (
    .addr(bit_extender_2_out), .we(reg_ex_mem_1_memwriteout), .oe(reg_ex_mem_1_memreadout), .clk(clk),
    .din(reg_ex_mem_1_rs2out), .dout(ram_1_dout));
  Reg_MEM_WB reg_mem_wb_1 (
    .RegWritein(reg_ex_mem_1_regwriteout), .MemtoRegin(MemToReg), .RDin(reg_ex_mem_1_rdout),
    .MemValuein(ram_1_dout), .ALUResin(AluRes), .CLK(clk), .RegWriteout(RegWrite),
    .MemtoRegout(reg_mem_wb_1_memtoregout), .RDout(reg_mem_wb_1_rdout),
    .MemValueout(reg_mem_wb_1_memvalueout), .ALUResout(reg_mem_wb_1_aluresout));
  Multiplexer #(.width(32)) multiplexer_8 (
    .in0(reg_mem_wb_1_aluresout), .in1(reg_mem_wb_1_memvalueout), .out(multiplexer_8_out),
    .sel(reg_mem_wb_1_memtoregout));

  // Notes on the sheet:
  //   contents of rom_1 (hex, n*v repeats v):
  //   0 ffffffa0 2 ffffff93 1 40 3 13 0 62 ffffff82 ffffffb3 0 50 20 23 0 0 23 ffffff83 0 ffffffa3
  //   ffffff83 ffffff93 2 ffffff82 ffffff82 ffffff93 0 53 ffffff94 63 fffffffe ffffff9f fffffff0 6f 0
  //   ffffffa3 ffffff83 ffffff93 0 70 22 23
endmodule

module ALU (
  input  [31:0] rs1,
  input  [31:0] seg_valor,
  input  [3:0] operation,
  output [31:0] ALU_Result
);

  wire [4:0] bit_extender_1_out;
  wire [31:0] adder_1_out, and_1_out, or_1_out, shifter_1_out, subtractor_1_out;

  Bit_Extender #(.in_width(32), .out_width(5)) bit_extender_1 (.in(seg_valor), .out(bit_extender_1_out));
  Adder #(.width(32)) adder_1 (.a(rs1), .b(seg_valor), .out(adder_1_out));  // open: cin, cout
  Subtractor #(.width(32)) subtractor_1 (.a(rs1), .b(seg_valor), .out(subtractor_1_out));  // open: bin, bout
  assign and_1_out = seg_valor & seg_valor;  // AND_Gate and_1, 32 bits wide
  assign or_1_out = rs1 | seg_valor;  // OR_Gate or_1, 32 bits wide
  Shifter #(.width(32)) shifter_1 (.in(rs1), .\dist (bit_extender_1_out), .out(shifter_1_out));
  Multiplexer #(.select(4), .width(32)) multiplexer_1 (
    .in0(and_1_out), .in1(or_1_out), .in2(adder_1_out), .in3(shifter_1_out), .in6(subtractor_1_out),
    .out(ALU_Result), .sel(operation));  // open: in4, in5, in7, in8, in9, in10, in11, in12, in13, in14, in15
endmodule

module IMM_Gen (
  input  [31:0] instrucao,
  input  MemWrite,
  input  Branch,
  output [31:0] saida
);

  wire [11:0] multiplexer_1_out, shifter_1_out;

  Shifter #(.shift("ar"), .width(12)) shifter_1 (
    .in({instrucao[31], instrucao[7], instrucao[30:25], instrucao[11:8]}), .\dist (4'b0001),
    .out(shifter_1_out));
  Multiplexer #(.select(2), .width(12)) multiplexer_1 (
    .in0(instrucao[31:20]), .in1({instrucao[31:25], instrucao[11:7]}), .in2(shifter_1_out),
    .out(multiplexer_1_out), .sel({Branch, MemWrite}));  // open: in3
  assign saida = {{20{multiplexer_1_out[11]}}, multiplexer_1_out};  // Bit_Extender bit_extender_1

  // Notes on the sheet:
  //   00: IMM Tipo I | 01: IMM Tipo S | 10: IMM Tipo B
endmodule

module Control (
  input  [6:0] opcode,
  output RegWrite,
  output Branch,
  output MemRead,
  output MemToReg,
  output MemWrite,
  output ALUSrc,
  output ALUOp0,
  output ALUOp1
);

  wire and_1_out, and_2_out, and_3_out, and_8_out, and_9_out;

  and and_1 (and_1_out, ~opcode[6], ~opcode[5], opcode[4], ~opcode[3], ~opcode[2], opcode[1], opcode[0]);  // AND_Gate
  and and_2 (and_2_out, ~opcode[6], ~opcode[5], ~opcode[4], ~opcode[3], ~opcode[2], opcode[1], opcode[0]);  // AND_Gate
  and and_3 (and_3_out, ~opcode[6], opcode[5], opcode[4], ~opcode[3], ~opcode[2], opcode[1], opcode[0]);  // AND_Gate
  and and_4 (Branch, opcode[6], opcode[5], ~opcode[4], ~opcode[3], ~opcode[2], opcode[1], opcode[0]);  // AND_Gate
  and and_5 (MemRead, ~opcode[6], ~opcode[5], ~opcode[4], ~opcode[3], ~opcode[2], opcode[1], opcode[0]);  // AND_Gate
  and and_6 (MemToReg, ~opcode[6], ~opcode[5], ~opcode[4], ~opcode[3], ~opcode[2], opcode[1], opcode[0]);  // AND_Gate
  and and_7 (MemWrite, ~opcode[6], opcode[5], ~opcode[4], ~opcode[3], ~opcode[2], opcode[1], opcode[0]);  // AND_Gate
  and and_8 (and_8_out, ~opcode[6], ~opcode[5], ~opcode[4], ~opcode[3], ~opcode[2], opcode[1], opcode[0]);  // AND_Gate
  and and_9 (and_9_out, ~opcode[6], opcode[5], ~opcode[4], ~opcode[3], ~opcode[2], opcode[1], opcode[0]);  // AND_Gate
  and and_10 (ALUOp0, opcode[6], opcode[5], ~opcode[4], ~opcode[3], ~opcode[2], opcode[1], opcode[0]);  // AND_Gate
  or or_1 (RegWrite, and_2_out, and_1_out, and_3_out);
  or or_2 (ALUSrc, and_8_out, and_1_out, and_9_out);
  and and_11 (ALUOp1, opcode[0], opcode[1], ~opcode[2], ~opcode[3], opcode[4], opcode[5], ~opcode[6]);  // AND_Gate
endmodule

module ALUCtrl (
  input  [6:0] Funct7,
  input  [2:0] Funct3,
  input  ALUOp1,
  input  ALUOp0,
  output [3:0] operation
);

  wire and_1_out, and_2_out, and_3_out, and_4_out, and_5_out, and_6_out, and_7_out, and_8_out, and_9_out;

  and and_1 (and_1_out, ~Funct7[0], ~Funct7[1], ~Funct7[2], ~Funct7[3], ~Funct7[4], ~Funct7[5], ~Funct7[6], Funct3[0], ~Funct3[1], ~Funct3[2], ~ALUOp1, ~ALUOp0);  // AND_Gate
  and and_2 (and_2_out, ALUOp1, ~ALUOp0);  // AND_Gate
  and and_3 (and_3_out, Funct3[1], Funct3[2], ~Funct7[0], ~Funct7[1], ~Funct7[2], ~Funct7[3], ~Funct7[4], ~Funct7[5], ~Funct7[6], ~Funct3[0], ~ALUOp0, ALUOp1);  // AND_Gate
  and and_4 (and_4_out, ~Funct3[1], ~Funct3[1], ~Funct3[0], ~Funct7[6], ~Funct7[5], ~Funct7[4], ~Funct7[3], ~Funct7[2], ~Funct7[1], ~Funct7[0], ~and_2_out, ALUOp1);  // AND_Gate
  and and_5 (and_5_out, ~Funct3[0], ~Funct3[1], ~Funct3[2], ~Funct7[0], ~Funct7[1], ~Funct7[2], ~Funct7[3], ~Funct7[4], Funct7[5], ~Funct7[6], ~ALUOp0, ALUOp1);  // AND_Gate
  or or_1 (operation[0], and_1_out, and_3_out);
  and and_6 (and_6_out, ~Funct3[2], ~and_4_out, ~Funct3[1]);  // AND_Gate
  and and_7 (and_7_out, and_5_out, and_2_out);
  and and_8 (and_8_out, ~ALUOp1, ALUOp0);  // AND_Gate
  or or_2 (operation[2], and_7_out, and_8_out);
  and and_9 (and_9_out, ~ALUOp1, ~ALUOp1);  // AND_Gate
  or or_3 (operation[1], and_6_out, and_9_out);

  assign operation[3] = 1'b0;
endmodule

module Reg_IF_ID (
  input  Enable,
  input  BranchStall,
  input  [23:0] PCin,
  input  [31:0] Instin,
  input  CLK,
  output [23:0] PCout,
  output [31:0] Instout
);

  wire [23:0] multiplexer_1_out;
  wire [31:0] multiplexer_2_out;

  Multiplexer #(.width(24)) multiplexer_1 (.in0(PCin), .in1({24{1'b0}}), .out(multiplexer_1_out), .sel(BranchStall));
  Multiplexer #(.width(32)) multiplexer_2 (.in0(Instin), .in1(32'h13), .out(multiplexer_2_out), .sel(BranchStall));
  Register #(.width(24)) register_1 (.D(multiplexer_1_out), .en(Enable), .clk(CLK), .Q(PCout));  // open: clr
  Register #(.width(32)) register_2 (.D(multiplexer_2_out), .en(Enable), .clk(CLK), .Q(Instout));  // open: clr
endmodule

module Reg_ID_EX (
  input  STALL,
  input  RegWritein,
  input  MemReadin,
  input  MemtoRegin,
  input  MemWritein,
  input  ALUSrcin,
  input  ALUOp0in,
  input  ALUOp1in,
  input  [4:0] RDin,
  input  [31:0] RS1Datain,
  input  [31:0] RS2Datain,
  input  [31:0] IMMin,
  input  [6:0] Funct7in,
  input  [2:0] Fucnt3in,
  input  [4:0] RS1in,
  input  [4:0] RS2in,
  input  CLK,
  output RegWriteout,
  output MemReadout,
  output MemtoRegout,
  output MemWriteout,
  output ALUSrcout,
  output ALUOp0out,
  output ALUOp1out,
  output [4:0] RDout,
  output [31:0] RS1Dataout,
  output [31:0] RS2Dataout,
  output [31:0] IMMout,
  output [6:0] Funct7out,
  output [2:0] Funct3out,
  output [4:0] RS1out,
  output [4:0] RS2out
);

  wire multiplexer_1_out, multiplexer_2_out, multiplexer_3_out, multiplexer_4_out, multiplexer_5_out,
       multiplexer_6_out, multiplexer_7_out;
  wire [2:0] multiplexer_12_out;
  wire [4:0] multiplexer_8_out, multiplexer_13_out, multiplexer_14_out;
  wire [6:0] multiplexer_11_out;
  wire [31:0] multiplexer_9_out, multiplexer_10_out;

  Multiplexer multiplexer_1 (.in0(RegWritein), .in1(1'b1), .out(multiplexer_1_out), .sel(STALL));
  Multiplexer multiplexer_2 (.in0(MemReadin), .in1(1'b0), .out(multiplexer_2_out), .sel(STALL));
  Multiplexer multiplexer_3 (.in0(MemtoRegin), .in1(1'b0), .out(multiplexer_3_out), .sel(STALL));
  Multiplexer multiplexer_4 (.in0(MemWritein), .in1(1'b0), .out(multiplexer_4_out), .sel(STALL));
  Multiplexer multiplexer_5 (.in0(ALUSrcin), .in1(1'b0), .out(multiplexer_5_out), .sel(STALL));
  Multiplexer multiplexer_6 (.in0(ALUOp0in), .in1(1'b0), .out(multiplexer_6_out), .sel(STALL));
  Multiplexer multiplexer_7 (.in0(ALUOp1in), .in1(1'b0), .out(multiplexer_7_out), .sel(STALL));
  Multiplexer #(.width(5)) multiplexer_8 (.in0(RDin), .in1({5{1'b0}}), .out(multiplexer_8_out), .sel(STALL));
  Multiplexer #(.width(32)) multiplexer_9 (.in0(RS1Datain), .in1({32{1'b0}}), .out(multiplexer_9_out), .sel(STALL));
  Multiplexer #(.width(32)) multiplexer_10 (.in0(IMMin), .in1({32{1'b0}}), .out(multiplexer_10_out), .sel(STALL));
  Multiplexer #(.width(7)) multiplexer_11 (.in0(Funct7in), .in1({7{1'b0}}), .out(multiplexer_11_out), .sel(STALL));
  Multiplexer #(.width(3)) multiplexer_12 (.in0(Fucnt3in), .in1(3'b000), .out(multiplexer_12_out), .sel(STALL));
  Multiplexer #(.width(5)) multiplexer_13 (.in0(RS1in), .in1({5{1'b0}}), .out(multiplexer_13_out), .sel(STALL));
  Multiplexer #(.width(5)) multiplexer_14 (.in0(RS2in), .in1({5{1'b0}}), .out(multiplexer_14_out), .sel(STALL));
  D_Flip_Flop d_ff_1 (.D(multiplexer_1_out), .clk(CLK), .Q(RegWriteout));  // open: Qn, preset, reset
  D_Flip_Flop d_ff_2 (.D(multiplexer_2_out), .clk(CLK), .Q(MemReadout));  // open: Qn, preset, reset
  D_Flip_Flop d_ff_3 (.D(multiplexer_3_out), .clk(CLK), .Q(MemtoRegout));  // open: Qn, preset, reset
  D_Flip_Flop d_ff_4 (.D(multiplexer_4_out), .clk(CLK), .Q(MemWriteout));  // open: Qn, preset, reset
  D_Flip_Flop d_ff_5 (.D(multiplexer_5_out), .clk(CLK), .Q(ALUSrcout));  // open: Qn, preset, reset
  D_Flip_Flop d_ff_6 (.D(multiplexer_6_out), .clk(CLK), .Q(ALUOp0out));  // open: Qn, preset, reset
  D_Flip_Flop d_ff_7 (.D(multiplexer_7_out), .clk(CLK), .Q(ALUOp1out));  // open: Qn, preset, reset
  Register #(.width(5)) register_1 (.D(multiplexer_8_out), .en(1'b1), .clk(CLK), .Q(RDout));  // open: clr
  Register #(.width(32)) register_2 (.D(multiplexer_9_out), .en(1'b1), .clk(CLK), .Q(RS1Dataout));  // open: clr
  Register #(.width(32)) register_3 (.D(RS2Datain), .en(1'b1), .clk(CLK), .Q(RS2Dataout));  // open: clr
  Register #(.width(32)) register_4 (.D(multiplexer_10_out), .en(1'b1), .clk(CLK), .Q(IMMout));  // open: clr
  Register #(.width(7)) register_5 (.D(multiplexer_11_out), .en(1'b1), .clk(CLK), .Q(Funct7out));  // open: clr
  Register #(.width(3)) register_6 (.D(multiplexer_12_out), .en(1'b1), .clk(CLK), .Q(Funct3out));  // open: clr
  Register #(.width(5)) register_7 (.D(multiplexer_13_out), .en(1'b1), .clk(CLK), .Q(RS1out));  // open: clr
  Register #(.width(5)) register_8 (.D(multiplexer_14_out), .en(1'b1), .clk(CLK), .Q(RS2out));  // open: clr
endmodule

module Reg_EX_MEM (
  input  RegWritein,
  input  MemReadin,
  input  MemtoRegin,
  input  MemWritein,
  input  [4:0] RDin,
  input  [31:0] ALUResin,
  input  [31:0] RS2in,
  input  CLK,
  output RegWriteout,
  output MemReadout,
  output MemtoRegout,
  output MemWriteout,
  output [4:0] RDout,
  output [31:0] ALUResout,
  output [31:0] RS2out
);

  D_Flip_Flop d_ff_1 (.D(RegWritein), .clk(CLK), .Q(RegWriteout));  // open: Qn, preset, reset
  D_Flip_Flop d_ff_2 (.D(MemReadin), .clk(CLK), .Q(MemReadout));  // open: Qn, preset, reset
  D_Flip_Flop d_ff_3 (.D(MemtoRegin), .clk(CLK), .Q(MemtoRegout));  // open: Qn, preset, reset
  D_Flip_Flop d_ff_4 (.D(MemWritein), .clk(CLK), .Q(MemWriteout));  // open: Qn, preset, reset
  Register #(.width(5)) register_1 (.D(RDin), .en(1'b1), .clk(CLK), .Q(RDout));  // open: clr
  Register #(.width(32)) register_2 (.D(ALUResin), .en(1'b1), .clk(CLK), .Q(ALUResout));  // open: clr
  Register #(.width(32)) register_3 (.D(RS2in), .en(1'b1), .clk(CLK), .Q(RS2out));  // open: clr
endmodule

module Reg_MEM_WB (
  input  RegWritein,
  input  MemtoRegin,
  input  [4:0] RDin,
  input  [31:0] MemValuein,
  input  [31:0] ALUResin,
  input  CLK,
  output RegWriteout,
  output MemtoRegout,
  output [4:0] RDout,
  output [31:0] MemValueout,
  output [31:0] ALUResout
);

  D_Flip_Flop d_ff_1 (.D(RegWritein), .clk(CLK), .Q(RegWriteout));  // open: Qn, preset, reset
  D_Flip_Flop d_ff_2 (.D(MemtoRegin), .clk(CLK), .Q(MemtoRegout));  // open: Qn, preset, reset
  Register #(.width(5)) register_1 (.D(RDin), .en(1'b1), .clk(CLK), .Q(RDout));  // open: clr
  Register #(.width(32)) register_2 (.D(MemValuein), .en(1'b1), .clk(CLK), .Q(MemValueout));  // open: clr
  Register #(.width(32)) register_3 (.D(ALUResin), .en(1'b1), .clk(CLK), .Q(ALUResout));  // open: clr
endmodule

module Forwarding_Control (
  input  [4:0] RS1,
  input  [4:0] RDWB,
  input  RegWriteWB,
  input  [4:0] RDMEM,
  input  REGWriteMEM,
  input  [4:0] RS2,
  output [1:0] Forward1,
  output [1:0] Forward2
);

  wire and_1_out, and_2_out, and_3_out, and_4_out, comparator_1_eq, comparator_2_eq, comparator_3_eq,
       comparator_4_eq, comparator_5_eq, comparator_6_eq;

  Comparator #(.width(5)) comparator_1 (.a(RS1), .b(RDWB), .eq(comparator_1_eq));  // open: gt, lt
  Comparator #(.width(5)) comparator_2 (.a(RDWB), .b(RS2), .eq(comparator_2_eq));  // open: gt, lt
  Comparator #(.width(5)) comparator_3 (.a(RS1), .b(RDMEM), .eq(comparator_3_eq));  // open: gt, lt
  Comparator #(.width(5)) comparator_4 (.a(RDMEM), .b(RS2), .eq(comparator_4_eq));  // open: gt, lt
  Comparator #(.width(5)) comparator_5 (.a({5{1'b0}}), .b(RDWB), .eq(comparator_5_eq));  // open: gt, lt
  Comparator #(.width(5)) comparator_6 (.a({5{1'b0}}), .b(RDMEM), .eq(comparator_6_eq));  // open: gt, lt
  and and_1 (and_1_out, comparator_1_eq, ~comparator_5_eq);  // AND_Gate
  and and_2 (and_2_out, ~comparator_5_eq, comparator_2_eq);  // AND_Gate
  and and_3 (and_3_out, comparator_3_eq, ~comparator_6_eq);  // AND_Gate
  and and_4 (and_4_out, ~comparator_6_eq, comparator_4_eq);  // AND_Gate
  and and_5 (Forward1[0], and_1_out, RegWriteWB);
  and and_6 (Forward2[0], RegWriteWB, and_2_out);
  and and_7 (Forward1[1], and_3_out, REGWriteMEM);
  and and_8 (Forward2[1], REGWriteMEM, and_4_out);
endmodule

module Hazard_Detection (
  input  [4:0] RS1,
  input  MemRead,
  input  [4:0] RDMem,
  input  [4:0] RS2,
  output STALL
);

  wire comparator_1_eq, comparator_2_eq, or_1_out;

  Comparator #(.width(5)) comparator_1 (.a(RS1), .b(RDMem), .eq(comparator_1_eq));  // open: gt, lt
  Comparator #(.width(5)) comparator_2 (.a(RDMem), .b(RS2), .eq(comparator_2_eq));  // open: gt, lt
  or or_1 (or_1_out, comparator_1_eq, comparator_2_eq);
  and and_1 (STALL, MemRead, or_1_out);
endmodule

module Control_Hazard_Detector (
  input  [6:0] OPcode,
  input  [4:0] RS1,
  input  [4:0] RDID,
  input  [4:0] RS2,
  input  RegWrite,
  input  MEMtoRegID,
  input  [4:0] RDEX,
  input  MEMtoRegEX,
  output STALL
);

  wire and_1_out, and_2_out, and_3_out, and_4_out, and_5_out, and_6_out, comparator_1_eq, comparator_2_eq,
       comparator_3_eq, comparator_4_eq, comparator_5_eq, or_1_out, or_2_out, or_3_out, or_4_out;

  Comparator #(.width(7)) comparator_1 (.a(7'b1100011), .b(OPcode), .eq(comparator_1_eq));  // open: gt, lt
  Comparator #(.width(5)) comparator_2 (.a(RS1), .b(RDID), .eq(comparator_2_eq));  // open: gt, lt
  Comparator #(.width(5)) comparator_3 (.a(RDID), .b(RS2), .eq(comparator_3_eq));  // open: gt, lt
  Comparator #(.width(5)) comparator_4 (.a({5{1'b0}}), .b(RDID), .eq(comparator_4_eq));  // open: gt, lt
  Comparator #(.width(5)) comparator_5 (.a({5{1'b0}}), .b(RDEX), .eq(comparator_5_eq));  // open: gt, lt
  and and_1 (and_1_out, comparator_2_eq, ~comparator_4_eq);  // AND_Gate
  and and_2 (and_2_out, ~comparator_4_eq, comparator_3_eq);  // AND_Gate
  and and_3 (and_3_out, comparator_2_eq, ~comparator_5_eq);  // AND_Gate
  and and_4 (and_4_out, ~comparator_5_eq, comparator_3_eq);  // AND_Gate
  or or_1 (or_1_out, and_1_out, and_2_out);
  or or_2 (or_2_out, RegWrite, MEMtoRegID);
  or or_3 (or_3_out, and_3_out, and_4_out);
  and and_5 (and_5_out, or_1_out, or_2_out);
  and and_6 (and_6_out, or_3_out, MEMtoRegEX);
  or or_4 (or_4_out, and_5_out, and_6_out);
  and and_7 (STALL, comparator_1_eq, or_4_out);
endmodule

module Overwrite_Forwarding (
  input  RegWrite,
  input  [4:0] RS1,
  input  [4:0] RD,
  input  [4:0] RS2,
  output FWD1,
  output FWD2
);

  wire and_1_out, and_2_out, comparator_1_eq, comparator_2_eq, comparator_3_eq;

  Comparator #(.width(5)) comparator_1 (.a(RS1), .b(RD), .eq(comparator_1_eq));  // open: gt, lt
  Comparator #(.width(5)) comparator_2 (.a(RD), .b(RS2), .eq(comparator_2_eq));  // open: gt, lt
  Comparator #(.width(5)) comparator_3 (.a({5{1'b0}}), .b(RD), .eq(comparator_3_eq));  // open: gt, lt
  and and_1 (and_1_out, comparator_1_eq, ~comparator_3_eq);  // AND_Gate
  and and_2 (and_2_out, ~comparator_3_eq, comparator_2_eq);  // AND_Gate
  and and_3 (FWD1, RegWrite, and_1_out);
  and and_4 (FWD2, RegWrite, and_2_out);
endmodule
